// Logisim project main.circ as structural Verilog: 1 circuit, main circuit main
module main (
);

  wire A_READ, A_WRITE, adder_1_cout, ALU_READ, ALU_WRITE, and_2_out, and_3_out, and_4_out, and_5_out,
       and_6_out, and_7_out, and_9_out, B_READ, B_WRITE, button_1_out, C_READ, C_WRITE, CARRY, CLK, IR_WRITE,
       MAR_READ, MAR_WRITE, nor_1_out, not_1_out, not_2_out, not_3_out, not_4_out, or_1_out, or_2_out,
       OUT_WRITE, PC_COUNT, PC_READ_A, PC_WRITE, RAM_ADDR_SEL, RAM_READ, RAM_WRITE, READ_EN, RESET,
       SEG_WRITE, subtractor_1_bout, ZERO;
  wire [1:0] comparator_1_eq;
  wire [2:0] controlled_buffer_5_out, PORT_SEL;
  wire [4:0] controlled_buffer_5_out_2;
  wire [6:0] ram_1_data;
  wire [7:0] A_q, adder_1_out, ALU_q, B_q, C_q, controlled_buffer_4_out, IR_q, MAR_q, multiplexer_1_out,
       multiplexer_2_out, nand_1_out, or_6_out, PC_q, pull_resistor_3_node, pull_resistor_4_node,
       pull_resistor_5_node, SEG_q, shifter_1_out, subtractor_1_out;
  wire [7:7] ram_1_data_2;

  Register SEG (.D({ram_1_data_2[7], ram_1_data}), .en(SEG_WRITE), .clk(CLK), .Q(SEG_q), .clr(RESET));
  Register MAR (.D({ram_1_data_2[7], ram_1_data}), .en(MAR_WRITE), .clk(CLK), .Q(MAR_q));  // open: clr
  Clock clock_1 (.out(CLK));
  Button button_1 (.out(button_1_out));
  Counter PC (
    .load(PC_WRITE), .D({ram_1_data_2[7], ram_1_data}), .count(PC_COUNT), .Q(PC_q), .clk(CLK), .clr(or_1_out));  // open: carry, up
  or or_1 (or_1_out, RESET, SEG_WRITE);
  and and_1 (RESET, CLK, button_1_out);
  Multiplexer #(.enable("false"), .width(8)) multiplexer_1 (
    .in0(PC_q), .in1(MAR_q), .out(multiplexer_1_out), .sel(RAM_ADDR_SEL));
  TTY tty_1 (.data(ram_1_data), .clk(CLK), .we(OUT_WRITE), .clr(RESET));
  RAM #(.addrWidth(16), .databus("bidir"), .readbehav("war"), .trigger("falling"), .\type ("nonvolatile")) ram_1 (
    .addr({SEG_q, multiplexer_1_out}), .we(RAM_WRITE), .oe(RAM_READ), .clk(CLK),
    .data({ram_1_data_2[7], ram_1_data}));
  or or_2 (or_2_out, PC_READ_A, IR_WRITE);
  D_Flip_Flop d_ff_1 (.D(READ_EN), .clk(CLK), .Q(IR_WRITE), .Qn(READ_EN), .preset(RESET));  // open: reset
  not not_1 (not_1_out, or_2_out);
  or or_3 (RAM_ADDR_SEL, RAM_WRITE, and_2_out);
  and and_2 (and_2_out, not_1_out, MAR_READ);
  or or_4 (RAM_READ, or_2_out, MAR_READ);
  // Probe on {ram_1_data_2[7], ram_1_data}
  or or_5 (PC_COUNT, IR_WRITE, and_3_out);
  and and_3 (and_3_out, READ_EN, PC_READ_A);
  Register IR (
    .D({ram_1_data_2[7], ram_1_data}), .en(IR_WRITE), .clk(CLK), .Q({IR_q[7:6], PORT_SEL, IR_q[2:0]}));  // open: clr
  Pull_Resistor pull_resistor_1 (.node({ram_1_data_2[7], ram_1_data}));
  Register A (.D({ram_1_data_2[7], ram_1_data}), .en(A_WRITE), .clk(CLK), .Q(A_q));  // open: clr
  Register B (.D({ram_1_data_2[7], ram_1_data}), .en(B_WRITE), .clk(CLK), .Q(B_q));  // open: clr
  Register C (.D({ram_1_data_2[7], ram_1_data}), .en(C_WRITE), .clk(CLK), .Q(C_q));  // open: clr
  Register ALU (.D({ram_1_data_2[7], ram_1_data}), .en(ALU_WRITE), .clk(CLK), .Q(ALU_q));  // open: clr
  assign {ram_1_data_2[7], ram_1_data} = A_READ ? A_q : 8'bz;  // Controlled_Buffer controlled_buffer_1
  assign {ram_1_data_2[7], ram_1_data} = B_READ ? B_q : 8'bz;  // Controlled_Buffer controlled_buffer_2
  assign {ram_1_data_2[7], ram_1_data} = C_READ ? C_q : 8'bz;  // Controlled_Buffer controlled_buffer_3
  not not_2 (not_2_out, ZERO);
  not not_3 (not_3_out, CARRY);
  assign controlled_buffer_4_out = ALU_q[3] ? A_q : 8'bz;  // Controlled_Buffer controlled_buffer_4
  assign {controlled_buffer_5_out_2, controlled_buffer_5_out} = ALU_q[2] ? C_q : 8'bz;  // Controlled_Buffer controlled_buffer_5
  // Probe on IR_q[2:0]
  // Probe on PORT_SEL
  and and_4 (and_4_out, IR_q[6], not_2_out);
  and and_5 (and_5_out, IR_q[7], not_3_out);
  and and_6 (and_6_out, IR_q[6], IR_q[7]);
  Pull_Resistor pull_resistor_2 (.node(controlled_buffer_4_out));
  Pull_Resistor pull_resistor_3 (.node(pull_resistor_3_node));
  assign pull_resistor_3_node = ALU_q[4] ? B_q : 8'bz;  // Controlled_Buffer controlled_buffer_6
  Pull_Resistor pull_resistor_4 (.node(pull_resistor_4_node));
  assign pull_resistor_4_node = ALU_q[5] ? A_q : 8'bz;  // Controlled_Buffer controlled_buffer_7
  Pull_Resistor pull_resistor_5 (.node(pull_resistor_5_node));
  assign pull_resistor_5_node = ALU_q[6] ? B_q : 8'bz;  // Controlled_Buffer controlled_buffer_8
  nor nor_1 (nor_1_out, and_4_out, and_5_out);
  and and_7 (and_7_out, nor_1_out, READ_EN);
  and and_8 (OUT_WRITE, READ_EN, and_6_out);
  assign or_6_out = controlled_buffer_4_out | pull_resistor_3_node;  // OR_Gate or_6, 8 bits wide
  assign {controlled_buffer_5_out_2, controlled_buffer_5_out} = pull_resistor_4_node | pull_resistor_5_node;  // OR_Gate or_7, 8 bits wide
  not not_4 (not_4_out, OUT_WRITE);
  assign {ram_1_data_2[7], ram_1_data} = ALU_READ ? multiplexer_2_out : 8'bz;  // Controlled_Buffer controlled_buffer_9
  Adder adder_1 (
    .a(or_6_out), .b({controlled_buffer_5_out_2, controlled_buffer_5_out}), .out(adder_1_out),
    .cin(ALU_q[7]), .cout(adder_1_cout));
  Subtractor subtractor_1 (
    .a(or_6_out), .b({controlled_buffer_5_out_2, controlled_buffer_5_out}), .out(subtractor_1_out),
    .bin(ALU_q[7]), .bout(subtractor_1_bout));
  assign nand_1_out = ~(or_6_out & {controlled_buffer_5_out_2, controlled_buffer_5_out});  // NAND_Gate nand_1, 8 bits wide
  Shifter #(.shift("lr")) shifter_1 (.in(or_6_out), .\dist (controlled_buffer_5_out), .out(shifter_1_out));
  Decoder #(.select(3)) decoder_1 (
    .out1(PC_READ_A), .out2(MAR_READ), .out3(A_READ), .out4(B_READ), .out5(C_READ), .out6(ALU_READ),
    .sel(IR_q[2:0]), .en(READ_EN));  // open: out0, out7
  and and_9 (and_9_out, and_7_out, not_4_out);
  Decoder #(.select(3)) decoder_2 (
    .out0(RAM_WRITE), .out1(PC_WRITE), .out2(MAR_WRITE), .out3(A_WRITE), .out4(B_WRITE), .out5(C_WRITE),
    .out6(ALU_WRITE), .out7(SEG_WRITE), .sel(PORT_SEL), .en(and_9_out));
  // Probe on multiplexer_2_out
  Multiplexer #(.enable("false"), .select(2), .width(8)) multiplexer_2 (
    .in0(adder_1_out), .in1(subtractor_1_out), .in2(nand_1_out), .in3(shifter_1_out),
    .out(multiplexer_2_out), .sel(ALU_q[1:0]));
  // Probe on ALU_q[1:0]
  Multiplexer #(.enable("false"), .select(2)) multiplexer_3 (
    .in0(adder_1_cout), .in1(subtractor_1_bout), .out(comparator_1_eq[1]), .sel(ALU_q[1:0]));  // open: in2, in3
  Comparator comparator_1 (.a(multiplexer_2_out), .b({8{1'b0}}), .eq(comparator_1_eq[0]));  // open: gt, lt
  Register #(.trigger("high"), .width(2)) F (
    .D(comparator_1_eq), .en(ALU_WRITE), .clk(CLK), .Q({CARRY, ZERO}));  // open: clr

  // Other names for the same wires on the sheet: PC_READ_B = IR_WRITE; PC_SEL = IR_WRITE; WRITE_EN = READ_EN
endmodule
